# Fritzing sketch explorer_pin_entry (saved by Fritzing 0.9.1b)

parts:
  U1 = Explorer HAT Pro [part_number="Explorer HAT Pro" package=THT]
  LED2 = LED - 5mm [color="Green (560nm)" package="5 mm [THT]"]  # not connected
  LED3 = LED - 5mm [color="Red (633nm)" package="5 mm [THT]"]  # not connected
  R1 = Resistor [tolerance=±5% resistance=470 package=THT]  # not connected
  R3 = Resistor [tolerance=±5% resistance=470 package=THT]  # not connected
  R4 = Resistor [tolerance=±5% resistance=470 package=THT]  # not connected

nets:
  N1: U1.5v, U1.G4, U1.G8, U1.H1, U1.H4, U1.H8, U1.I1, U1.J1
  N2: U1.C3, U1.E3, U1.Output_1
  N3: U1.C4, U1.E4
  N4: U1.C7, U1.E7, U1.Output_2
  N5: U1.C8, U1.E8
  N6: U1.G12, U1.I12, U1.J12, U1.Ground
  N7: U1.I16, U1.J16, U1.PWM

custom parts:
  Explorer HAT Pro: Explorer HAT Pro with 4 Output and 4 Input connections, 4 Analog Inputs and 2 bi-directional motor channels, plus power and ground.
