# Fritzing sketch explorer_shift_register (saved by Fritzing 0.9.1b)
breadboards: 1

parts:
  U3 = Explorer HAT Pro [part_number="Explorer HAT Pro" package=THT]
  LED12 = smd LED [color="Red (633nm)" package="1206 [SMD]"]
  LED13 = smd LED [color="Red (633nm)" package="1206 [SMD]"]
  LED14 = smd LED [color="Red (633nm)" package="1206 [SMD]"]
  LED15 = smd LED [color="Red (633nm)" package="1206 [SMD]"]
  LED16 = smd LED [color="Red (633nm)" package="1206 [SMD]"]
  LED17 = smd LED [color="Red (633nm)" package="1206 [SMD]"]
  LED18 = smd LED [color="Red (633nm)" package="1206 [SMD]"]
  LED19 = smd LED [color="Red (633nm)" package="1206 [SMD]"]
  R15 = Resistor [tolerance=±5% resistance=470 package="0603 [SMD]"]
  R16 = Resistor [tolerance=±5% resistance=470 package="0603 [SMD]"]
  R17 = Resistor [tolerance=±5% resistance=470 package="0603 [SMD]"]
  R18 = Resistor [tolerance=±5% resistance=470 package="0603 [SMD]"]
  R19 = Resistor [tolerance=±5% resistance=470 package="0603 [SMD]"]
  R20 = Resistor [tolerance=±5% resistance=470 package="0603 [SMD]"]
  R21 = Resistor [tolerance=±5% resistance=470 package="0603 [SMD]"]
  R22 = Resistor [tolerance=±5% resistance=470 package="0603 [SMD]"]
  Raspberry_Pi2 = Raspberry Pi B+  # not connected
  R23 = Resistor [tolerance=±5% resistance=10k package=THT]  # not connected
  U4 = 74HC595 SMD [package="SO16 [SMD]"]  # not connected
  R24 = Resistor [tolerance=±5% resistance=10k package=THT]  # not connected
  R25 = Resistor [tolerance=±5% resistance=10k package=THT]  # not connected

nets:
  N1: U3.5v, U3.F6, U3.F12, U3.G15, U3.G16, U3.G17, U3.H12, U3.H15, U3.H16, U3.H17, U3.I6, U3.I12, U3.I15, U3.I16, U3.J6
  N2: U3.A1, U3.A5, U3.D1, U3.D5, U3.E1, U3.E5, U3.F1, U3.F9, U3.H1, U3.H9, U3.J9, U3.Ground, R15.Pin_0, R16.Pin_0, R17.Pin_0, R18.Pin_0, R19.Pin_0, R20.Pin_0, R21.Pin_0, R22.Pin_0
  N3: U3.A2, U3.B2
  N4: U3.A4, U3.B4
  N5: U3.A6, U3.D6, U3.E6, LED12.anode
  N6: U3.A7, U3.D7, U3.E7, LED13.anode
  N7: U3.A8, U3.D8, U3.E8, LED14.anode
  N8: U3.A9, U3.D9, U3.E9, LED15.anode
  N9: U3.A10, U3.D10, U3.E10, LED16.anode
  N10: U3.A11, U3.D11, U3.E11, LED17.anode
  N11: U3.A12, U3.D12, U3.E12, LED18.anode
  N12: U3.A13, U3.B13
  N13: U3.A14, U3.B14
  N14: U3.A15, U3.D15, U3.E15, U3.F10, U3.G10, U3.J10, U3.Output_3
  N15: U3.A16, U3.C16, U3.E16, U3.F8, U3.G8, U3.J8, U3.Output_2
  N16: U3.A17, U3.B17, U3.E17, U3.F7, U3.G7, U3.J7, U3.Output_1
  N17: U3.F11, U3.G11, LED19.anode
  N18: LED12.cathode, R21.Pin_1
  N19: LED13.cathode, R20.Pin_1
  N20: LED14.cathode, R22.Pin_1
  N21: LED15.cathode, R19.Pin_1
  N22: LED16.cathode, R15.Pin_1
  N23: LED17.cathode, R18.Pin_1
  N24: LED18.cathode, R16.Pin_1
  N25: LED19.cathode, R17.Pin_1

custom parts:
  Explorer HAT Pro: Explorer HAT Pro with 4 Output and 4 Input connections, 4 Analog Inputs and 2 bi-directional motor channels, plus power and ground.
